# Fritzing sketch schematics (saved by Fritzing 0.8.5b)

parts:
  LED1 = LED - 5mm [color="Red (633nm)" package="5 mm [THT]"]
  R1 = Resistor [tolerance=±5% resistance=220 package=THT]
  LED2 = LED - 5mm [color="Red (633nm)" package="5 mm [THT]"]
  R2 = Resistor [tolerance=±5% resistance=220 package=THT]
  LED3 = LED - 5mm [color="Red (633nm)" package="5 mm [THT]"]
  LED4 = LED - 5mm [color="Red (633nm)" package="5 mm [THT]"]
  R3 = Resistor [tolerance=±5% resistance=220 package=THT]
  R4 = Resistor [tolerance=±5% resistance=220 package=THT]
  LED5 = LED - 5mm [color="Red (633nm)" package="5 mm [THT]"]
  LED6 = LED - 5mm [color="Red (633nm)" package="5 mm [THT]"]
  R5 = Resistor [tolerance=±5% resistance=220 package=THT]
  R6 = Resistor [tolerance=±5% resistance=220 package=THT]
  LED7 = LED - 5mm [color="Red (633nm)" package="5 mm [THT]"]
  LED8 = LED - 5mm [color="Red (633nm)" package="5 mm [THT]"]
  R7 = Resistor [tolerance=±5% resistance=220 package=THT]
  R8 = Resistor [tolerance=±5% resistance=220 package=THT]
  LED9 = LED - 5mm [color="Red (633nm)" package="5 mm [THT]"]
  LED10 = LED - 5mm [color="Red (633nm)" package="5 mm [THT]"]
  R9 = Resistor [tolerance=±5% resistance=220 package=THT]
  R10 = Resistor [tolerance=±5% resistance=220 package=THT]
  LED11 = LED - 5mm [color="Red (633nm)" package="5 mm [THT]"]
  LED12 = LED - 5mm [color="Red (633nm)" package="5 mm [THT]"]
  R11 = Resistor [tolerance=±5% resistance=220 package=THT]
  R12 = Resistor [tolerance=±5% resistance=220 package=THT]
  LED13 = LED - 5mm [color="Red (633nm)" package="5 mm [THT]"]
  LED14 = LED - 5mm [color="Red (633nm)" package="5 mm [THT]"]
  R13 = Resistor [tolerance=±5% resistance=220 package=THT]
  R14 = Resistor [tolerance=±5% resistance=220 package=THT]
  LED15 = LED - 5mm [color="Red (633nm)" package="5 mm [THT]"]
  LED16 = LED - 5mm [color="Red (633nm)" package="5 mm [THT]"]
  R15 = Resistor [tolerance=±5% resistance=220 package=THT]
  R16 = Resistor [tolerance=±5% resistance=220 package=THT]
  U1 = 74HC595 [package="DIP16 [THT]"]
  U2 = 74HC595 [package="DIP16 [THT]"]
  Part1 = Arduino Uno (Rev3)
  Part2 = Real Time Clock Module - DS1307 RTC Breakout Board
  S1 = Pushbutton [package="[THT]"]
  R17 = Resistor [tolerance=±5% resistance=220 package=THT]
  S2 = Pushbutton [package="[THT]"]
  R18 = Resistor [tolerance=±5% resistance=220 package=THT]

nets:
  GND: LED1.cathode, LED2.cathode, LED3.cathode, LED4.cathode, LED5.cathode, LED6.cathode, LED7.cathode, LED8.cathode, LED9.cathode, LED10.cathode, LED11.cathode, LED12.cathode, LED13.cathode, LED14.cathode, LED16.cathode, U1.GND, U1.OE, U2.GND, U2.OE, Part1.GND, Part2.GND, R17.Pin_1, R18.Pin_1
  N1: LED1.anode, R1.Pin_0
  N2: R1.Pin_1, U1.Q0
  N3: LED2.anode, R2.Pin_0
  N4: R2.Pin_1, U1.Q1
  N5: LED3.anode, R3.Pin_0
  N6: LED4.anode, R4.Pin_0
  N7: R3.Pin_1, U1.Q3
  N8: R4.Pin_1, U1.Q2
  N9: LED5.anode, R5.Pin_0
  N10: LED6.anode, R6.Pin_0
  N11: R5.Pin_1, U1.Q5
  N12: R6.Pin_1, U1.Q4
  N13: LED7.anode, R7.Pin_0
  N14: LED8.anode, R8.Pin_0
  N15: R7.Pin_1, U1.Q7
  N16: R8.Pin_1, U1.Q6
  N17: LED9.anode, R9.Pin_0
  N18: LED10.anode, R10.Pin_0
  N19: R9.Pin_1, U2.Q1
  N20: R10.Pin_1, U2.Q0
  N21: LED11.anode, R11.Pin_0
  N22: LED12.anode, R12.Pin_0
  N23: R11.Pin_1, U2.Q3
  N24: R12.Pin_1, U2.Q2
  N25: LED13.anode, R13.Pin_0
  N26: LED14.anode, R14.Pin_0
  N27: R13.Pin_1, U2.Q5
  N28: R14.Pin_1, U2.Q4
  N29: LED15.anode, R15.Pin_0
  N30: LED16.anode, R16.Pin_0
  N31: R15.Pin_1, U2.Q7
  N32: R16.Pin_1, U2.Q6
  VCC: U1.MR, U1.VCC, U2.MR, U2.VCC, Part1.5V, Part2.5V, S1.Pin_1, S2.Pin_1
  N33: U1.SH_CP, Part1.D4
  N34: U1.ST_CP, Part1.D3_PWM
  N35: U1.DS, Part1.D2
  N36: U2.SH_CP, Part1.D10_PWM/SS
  N37: U2.ST_CP, Part1.D9_PWM
  N38: U2.DS, Part1.D8
  N39: Part1.A4/SDA, Part2.SDA
  N40: Part1.A5/SCL, Part2.SCL
  N41: Part1.D5_PWM, S1.Pin_3, S1.Pin_4, R17.Pin_0
  N42: Part1.D6_PWM, S2.Pin_3, S2.Pin_4, R18.Pin_0
